# Fritzing sketch Fritzing_sketch (saved by Fritzing 0.9.9b)
circuit board: 8.46667cm x 5.64444cm
breadboards: 1

parts:
  M1 = DOIT Esp32 DevKit v1 (30 pins long, 11 pins width) [part_number=ESP32S-PIN30]
  Grove1 = Grove OLED 128x96
  RHT1 = Humidity and Temperature Sensor RHT03
  R1 = Rotary Potentiometer (Small) [maximum_resistance=100kΩ package=THT]
  HC-SR04_Sensor_1 = HC-SR04 Ultrasonic Distance Sensor
  Bauteil1 = PN532 Elechouse RFID NFC Module V3
  A1 = 1x18650 battery shield [package=THT]
  Module1 = Boladge HMC5883L Compass Module
  Sensor1 = Gas Sensor Breakout Board
  LED1 = smd LED [color="Red (633nm)" package="1206 [SMD]"]
  LED2 = smd LED [color="Yellow (595nm)" package="1206 [SMD]"]
  LED3 = smd LED [color="Green (570nm)" package="1206 [SMD]"]
  U1 = mystery part, 3 pins [chip_label="KY-039 Heartbeat"]
  S1 = SWITCH-SPST-2 [package=switch-spst-vertical]

nets:
  3V3: M1.3V3, R1.leg2, Module1.VCC, U1.pin2
  GND: M1.GND, Grove1.GND, RHT1.GND_2, R1.leg1, HC-SR04_Sensor_1.GND, Bauteil1.GND, A1.pin_1, A1.pin_5, A1.pin_8, A1.pin_12, Module1.GND, Sensor1.GND, LED2.cathode, LED3.cathode, U1.pin3
  N1: M1.D4, RHT1.Data-signal
  N2: M1.D5, LED2.anode
  N3: M1.D18, LED3.anode
  N4: M1.D19, LED1.anode
  N5: M1.D21, Grove1.SDA, Bauteil1.SDA, Module1.SDA
  N6: M1.D22, Grove1.SCL, Bauteil1.SCL, Module1.SCL
  N7: M1.VP, U1.pin1
  N8: M1.VN, Sensor1.DOUT
  N9: M1.D34, R1.wiper
  N10: M1.D14, HC-SR04_Sensor_1.TRIG
  N11: M1.D13, HC-SR04_Sensor_1.ECHO
  VCC: M1.VIN, Grove1.VCC, RHT1.Vcc, HC-SR04_Sensor_1.VCC, Bauteil1.VCC, Sensor1.5V, S1.P
  N12: A1.pin_7, A1.pin_11, S1.O

custom parts:
  DOIT Esp32 DevKit v1 (30 pins long, 11 pins width): The DOIT Esp32 DevKit v1 is one of the development board created by DOIT to evaluate the ESP-WROOM-32 module. It is based on the ESP32 microcontroller that boasts Wifi, Bluetooth, Ethernet and Low Power support all in a single chip. (vanepp) made breadboard work, adjusted pin numbering and labels and reduced size of schematic and cleaned up pcb. This chip is 30pins long (2 x15) and 11 pins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
  PN532 Elechouse RFID NFC Module V3: NFC is a popular technology in recent years. We often heard this work while smart phone company such as Samsung or HTC introduces their latest high-end phones. Almost all the high-end phone in the market support NFC. Near field communication (NFC) is a set of standards for smart phones and similar devices to establish radio communication with each other by touching them together or bringing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
  1x18650 battery shield: 1x18650 Lithium Battery Shield V3 CC CV Type-C Micro USB Mobile Power Bank DIY Module 5V 3A 3V 1A for iPhone Samsung Xiaomi.
  Boladge HMC5883L Compass Module: Cheap digital compass module
  Gas Sensor Breakout Board: Gas sensor breakout board. Input voltage is 5V. Sensor output is available in analog and digital.
